// Logisim project AsteroidPong.circ as structural Verilog: 17 circuits, main circuit main
module main (
);

  wire _128_HZ_out, GAME_OVER, GAnoUser, not_1_out;
  wire [3:0] PC1, PC2, U1, U2;
  wire [6:0] keyboard_1_data;
  wire [31:0] pantalla_gameover_1__0, pantalla_gameover_1__1, pantalla_gameover_1__2, pantalla_gameover_1__3,
       pantalla_gameover_1__4, tab_ajedres_1__0, tab_ajedres_1__1, worldprocess_1_f0, worldprocess_1_f1,
       worldprocess_1_f2, worldprocess_1_f3, worldprocess_1_f4, worldprocess_1_f5, worldprocess_1_f6,
       worldprocess_1_f7, worldprocess_1_f8, worldprocess_1_f9, worldprocess_1_f10, worldprocess_1_f11,
       worldprocess_1_f12, worldprocess_1_f13, worldprocess_1_f14, worldprocess_1_f15, worldprocess_1_f16,
       worldprocess_1_f17, worldprocess_1_f18, worldprocess_1_f19, worldprocess_1_f20, worldprocess_1_f21,
       worldprocess_1_f22, worldprocess_1_f23, worldprocess_1_f24, worldprocess_1_f25, worldprocess_1_f26,
       worldprocess_1_f27, worldprocess_1_f28, worldprocess_1_f29, worldprocess_1_f30, worldprocess_1_player;

  ScreenStart screenstart_1 ();  // open: F9, F10, F11, F12, F13, F14, F15, F16, F17, F18, F19, F20, F21
  Clock _128_HZ (.out(_128_HZ_out));
  Keyboard keyboard_1 (.clk(_128_HZ_out), .re(not_1_out), .data(keyboard_1_data));  // open: clr, avail
  not not_1 (not_1_out, GAME_OVER);
  TAb_AJEDRES tab_ajedres_1 (._0(tab_ajedres_1__0), ._1(tab_ajedres_1__1));
  WorldProcess worldprocess_1 (
    .GameOver(GAME_OVER), .in_2(_128_HZ_out), .in_3(keyboard_1_data), .F0(worldprocess_1_f0),
    .F1(worldprocess_1_f1), .F2(worldprocess_1_f2), .F3(worldprocess_1_f3), .F4(worldprocess_1_f4),
    .F5(worldprocess_1_f5), .F6(worldprocess_1_f6), .F7(worldprocess_1_f7), .F8(worldprocess_1_f8),
    .F9(worldprocess_1_f9), .F10(worldprocess_1_f10), .F11(worldprocess_1_f11), .F12(worldprocess_1_f12),
    .F13(worldprocess_1_f13), .F14(worldprocess_1_f14), .F15(worldprocess_1_f15), .F16(worldprocess_1_f16),
    .F17(worldprocess_1_f17), .F18(worldprocess_1_f18), .F19(worldprocess_1_f19), .F20(worldprocess_1_f20),
    .F21(worldprocess_1_f21), .F22(worldprocess_1_f22), .F23(worldprocess_1_f23), .F24(worldprocess_1_f24),
    .F25(worldprocess_1_f25), .F26(worldprocess_1_f26), .F27(worldprocess_1_f27), .F28(worldprocess_1_f28),
    .F29(worldprocess_1_f29), .F30(worldprocess_1_f30), .player(worldprocess_1_player));
  DotMatrix #(.inputtype("row"), .matrixcols(32), .matrixrows(32)) dotmatrix_1 (
    .row0(worldprocess_1_f0), .row1(worldprocess_1_f1), .row2(worldprocess_1_f2), .row3(worldprocess_1_f3),
    .row4(worldprocess_1_f4), .row5(worldprocess_1_f5), .row6(worldprocess_1_f6), .row7(worldprocess_1_f7),
    .row8(worldprocess_1_f8), .row9(worldprocess_1_f9), .row10(worldprocess_1_f10),
    .row11(worldprocess_1_f11), .row12(worldprocess_1_f12), .row13(worldprocess_1_f13),
    .row14(worldprocess_1_f14), .row15(worldprocess_1_f15), .row16(worldprocess_1_f16),
    .row17(worldprocess_1_f17), .row18(worldprocess_1_f18), .row19(worldprocess_1_f19),
    .row20(worldprocess_1_f20), .row21(worldprocess_1_f21), .row22(worldprocess_1_f22),
    .row23(worldprocess_1_f23), .row24(worldprocess_1_f24), .row25(worldprocess_1_f25),
    .row26(worldprocess_1_f26), .row27(worldprocess_1_f27), .row28(worldprocess_1_f28),
    .row29(worldprocess_1_f29), .row30(worldprocess_1_f30), .row31(worldprocess_1_player));
  DotMatrix #(.inputtype("row"), .matrixcols(32), .matrixrows(2), .dotshape("circle")) dotmatrix_2 (
    .row0(tab_ajedres_1__0), .row1(tab_ajedres_1__1));
  Pantalla_GAMEOVER pantalla_gameover_1 (
    .GAMEOVER(GAME_OVER), .GANOUSER(GAnoUser), ._0(pantalla_gameover_1__0), ._1(pantalla_gameover_1__1),
    ._2(pantalla_gameover_1__2), ._3(pantalla_gameover_1__3), ._4(pantalla_gameover_1__4));
  DotMatrix #(.inputtype("row"), .matrixcols(32), .matrixrows(5)) dotmatrix_3 (
    .row0(pantalla_gameover_1__0), .row1(pantalla_gameover_1__1), .row2(pantalla_gameover_1__2),
    .row3(pantalla_gameover_1__3), .row4(pantalla_gameover_1__4));
  ColisionCompleto colisioncompleto_1 (
    .Barra(worldprocess_1_player), .ULTIMA(worldprocess_1_f30), .u1(U1), .u2(U2), ._25(GAnoUser),
    .GAME_OVER(GAME_OVER), .Pc1(PC1), .pc2(PC2));
  Hex_Digit_Display hex_digit_display_1 (.value(U2));  // open: dp
  Hex_Digit_Display hex_digit_display_2 (.value(U1));  // open: dp
  Hex_Digit_Display hex_digit_display_3 (.value(PC1));  // open: dp
  Hex_Digit_Display hex_digit_display_4 (.value(PC2));  // open: dp

  // Notes on the sheet:
  //   ASTEROID PONG
  //   ASTEROID PONG
  //   ASTEROID PONG
  //   ASTEROID PONG
  //   Score:
  //   Player
  //   PC
  //   Intrucciones:
  //   el juego consiste en atrapar los asteoirdes
  //   con la barra inferior, la cual se controla con las teclas:
  //   "a"para movererse a la izquierda
  //   "d" para moverse a la derecha
  //   cada asteoide atrapado suma punto para el jugador
  //   y cada asteroide no atrapado suma punto para la maquina
  //   el ganador sera el primero en llegar a 25 puntos
  //   IMPORTANTE: frecuencia del rejoj  en 128
  //   y el teclado debe estar seleccionado
endmodule

module Player (
  input  [6:0] in_1,
  output [31:0] out_2,
  output out_3
);

  wire comparator_1_eq, comparator_2_eq, playermovselect_1_anterior, playermovselect_1_siguiente;
  wire [4:0] counter_1_q;

  Comparator #(.width(7), .mode("unsigned")) comparator_1 (
    .a(7'b1100001), .b(in_1), .eq(comparator_1_eq));  // open: gt, lt
  Comparator #(.width(7), .mode("unsigned")) comparator_2 (
    .a(7'b1100100), .b(in_1), .eq(comparator_2_eq));  // open: gt, lt
  Comparator #(.width(7), .mode("unsigned")) comparator_3 (.a(7'b1110010), .b(in_1), .eq(out_3));  // open: gt, lt
  PlayerMovSelect playermovselect_1 (
    .a(comparator_1_eq), .d(comparator_2_eq), .anterior(playermovselect_1_anterior),
    .siguiente(playermovselect_1_siguiente));
  Counter #(.width(5), .max('h1f)) counter_1 (
    .load(playermovselect_1_anterior), .Q(counter_1_q), .clk(playermovselect_1_siguiente));  // open: D, count, carry, clr
  PlayerMovement playermovement_1 (.in_1(counter_1_q), .out_2(out_2));
endmodule

module PlayerMovSelect (
  input  a,
  input  d,
  output anterior,
  output siguiente
);

  wire and_2_out, and_3_out, not_1_out, not_2_out, not_3_out;

  not not_1 (not_1_out, d);
  not not_2 (not_2_out, a);
  not not_3 (not_3_out, d);
  and and_1 (anterior, a, not_1_out);
  and and_2 (and_2_out, not_2_out, d);
  and and_3 (and_3_out, a, not_3_out);
  or or_1 (siguiente, and_2_out, and_3_out);
endmodule

// at
module RandomSystem (
  input  _2_a_la_3,
  output [7:0] _8
);

  wire [2:0] random_1_out;

  Random #(.width(3)) random_1 (.clk(_2_a_la_3), .next(1'b1), .out(random_1_out));  // open: clr
  Decoder #(.select(3)) decoder_1 (
    .out0(_8[7]), .out1(_8[6]), .out2(_8[5]), .out3(_8[4]), .out4(_8[3]), .out5(_8[2]), .out6(_8[1]),
    .out7(_8[0]), .sel(random_1_out));  // open: en
endmodule

module PlayerMovement (
  input  [4:0] in_1,
  output [31:0] out_2
);

  Multiplexer #(.select(5), .width(32)) multiplexer_1 (
    .in0(32'he0000000), .in1(32'h70000000), .in2(32'h38000000), .in3(32'h1c000000), .in4(32'he000000),
    .in5(32'h7000000), .in6(32'h3800000), .in7(32'h1c00000), .in8(32'he00000), .in9(32'h700000),
    .in10(32'h380000), .in11(32'h1c0000), .in12(32'he0000), .in13(32'h70000), .in14(32'h38000),
    .in15(32'h1c000), .in16(32'he000), .in17(32'h7000), .in18(32'h3800), .in19(32'h1c00), .in20(32'he00),
    .in21(32'h700), .in22(32'h380), .in23(32'h1c0), .in24(32'he0), .in25(32'h70), .in26(32'h38),
    .in27(32'h1c), .in28(32'he), .in29(32'h7), .in30(32'h80000003), .in31(32'hc0000001), .out(out_2),
    .sel(in_1));  // open: en
endmodule

module WorldProcess (
  input  GameOver,
  input  in_2,
  input  [6:0] in_3,
  output [31:0] F0,
  output [31:0] F1,
  output [31:0] F2,
  output [31:0] F3,
  output [31:0] F4,
  output [31:0] F5,
  output [31:0] F6,
  output [31:0] F7,
  output [31:0] F8,
  output [31:0] F9,
  output [31:0] F10,
  output [31:0] F11,
  output [31:0] F12,
  output [31:0] F13,
  output [31:0] F14,
  output [31:0] F15,
  output [31:0] F16,
  output [31:0] F17,
  output [31:0] F18,
  output [31:0] F19,
  output [31:0] F20,
  output [31:0] F21,
  output [31:0] F22,
  output [31:0] F23,
  output [31:0] F24,
  output [31:0] F25,
  output [31:0] F26,
  output [31:0] F27,
  output [31:0] F28,
  output [31:0] F29,
  output [31:0] F30,
  output [31:0] player
);

  wire and_1_out, clockprocessor_1_generar_dos, clockprocessor_1_generar_tres, clockprocessor_1_generar_uno,
       controlled_buffer_1_out, not_1_out, not_2_out, player_1_out_3;
  wire [4:0] clockprocessor_1_mover_dos, clockprocessor_1_mover_tres, clockprocessor_1_mover_uno;
  wire [31:0] bitselector_1_out, bitselector_2_out, bitselector_3_out, bitselector_4_out, bitselector_5_out,
       bitselector_6_out, bitselector_7_out, bitselector_8_out, bitselector_9_out, bitselector_10_out,
       bitselector_11_out, bitselector_12_out, bitselector_13_out, graphicchipset_1_f3, graphicchipset_1_f4,
       graphicchipset_1_f5, graphicchipset_1_f6, graphicchipset_1_f7, graphicchipset_1_f8,
       graphicchipset_1_f9, graphicchipset_1_f10, graphicchipset_1_f11, graphicchipset_1_f12,
       graphicchipset_1_f13, graphicchipset_1_f14, graphicchipset_1_f15, screenstart_1_f9, screenstart_1_f10,
       screenstart_1_f11, screenstart_1_f12, screenstart_1_f13, screenstart_1_f14, screenstart_1_f15,
       screenstart_1_f16, screenstart_1_f17, screenstart_1_f18, screenstart_1_f19, screenstart_1_f20,
       screenstart_1_f21;

  ScreenStart screenstart_1 (
    .F9(screenstart_1_f9), .F10(screenstart_1_f10), .F11(screenstart_1_f11), .F12(screenstart_1_f12),
    .F13(screenstart_1_f13), .F14(screenstart_1_f14), .F15(screenstart_1_f15), .F16(screenstart_1_f16),
    .F17(screenstart_1_f17), .F18(screenstart_1_f18), .F19(screenstart_1_f19), .F20(screenstart_1_f20),
    .F21(screenstart_1_f21));
  not not_1 (not_1_out, GameOver);
  BitSelector #(.width(32), .group(32)) bitselector_1 (.in(screenstart_1_f9), .out(bitselector_1_out), .sel(not_1_out));
  BitSelector #(.width(32), .group(32)) bitselector_2 (
    .in(screenstart_1_f10), .out(bitselector_2_out), .sel(not_1_out));
  BitSelector #(.width(32), .group(32)) bitselector_3 (
    .in(screenstart_1_f11), .out(bitselector_3_out), .sel(not_1_out));
  BitSelector #(.width(32), .group(32)) bitselector_4 (
    .in(screenstart_1_f12), .out(bitselector_4_out), .sel(not_1_out));
  BitSelector #(.width(32), .group(32)) bitselector_5 (
    .in(screenstart_1_f13), .out(bitselector_5_out), .sel(not_1_out));
  BitSelector #(.width(32), .group(32)) bitselector_6 (
    .in(screenstart_1_f14), .out(bitselector_6_out), .sel(not_1_out));
  BitSelector #(.width(32), .group(32)) bitselector_7 (
    .in(screenstart_1_f15), .out(bitselector_7_out), .sel(not_1_out));
  BitSelector #(.width(32), .group(32)) bitselector_8 (
    .in(screenstart_1_f16), .out(bitselector_8_out), .sel(not_1_out));
  BitSelector #(.width(32), .group(32)) bitselector_9 (
    .in(screenstart_1_f17), .out(bitselector_9_out), .sel(not_1_out));
  BitSelector #(.width(32), .group(32)) bitselector_10 (
    .in(screenstart_1_f18), .out(bitselector_10_out), .sel(not_1_out));
  BitSelector #(.width(32), .group(32)) bitselector_11 (
    .in(screenstart_1_f19), .out(bitselector_11_out), .sel(not_1_out));
  BitSelector #(.width(32), .group(32)) bitselector_12 (
    .in(screenstart_1_f20), .out(bitselector_12_out), .sel(not_1_out));
  BitSelector #(.width(32), .group(32)) bitselector_13 (
    .in(screenstart_1_f21), .out(bitselector_13_out), .sel(not_1_out));
  and and_1 (and_1_out, GameOver, player_1_out_3);
  not not_2 (not_2_out, GameOver);
  assign controlled_buffer_1_out = not_2_out ? in_2 : 1'bz;  // Controlled_Buffer controlled_buffer_1
  ClockProcessor clockprocessor_1 (
    .reloj(controlled_buffer_1_out), .generar_tres(clockprocessor_1_generar_tres),
    .generar_dos(clockprocessor_1_generar_dos), .generar_uno(clockprocessor_1_generar_uno),
    .mover_uno(clockprocessor_1_mover_uno), .mover_dos(clockprocessor_1_mover_dos),
    .mover_tres(clockprocessor_1_mover_tres));
  GraphicChipSet graphicchipset_1 (
    .mover_tercero(clockprocessor_1_mover_tres), .mover_primero(clockprocessor_1_mover_uno),
    .mover_segundo(clockprocessor_1_mover_dos), .generar_tercero(clockprocessor_1_generar_tres),
    .generar_segundo(clockprocessor_1_generar_dos), .generar_primero(clockprocessor_1_generar_uno), .F0(F0),
    .F1(F1), .F2(F2), .F3(graphicchipset_1_f3), .F4(graphicchipset_1_f4), .F5(graphicchipset_1_f5),
    .F6(graphicchipset_1_f6), .F7(graphicchipset_1_f7), .F8(graphicchipset_1_f8), .F9(graphicchipset_1_f9),
    .F10(graphicchipset_1_f10), .F11(graphicchipset_1_f11), .F12(graphicchipset_1_f12),
    .F13(graphicchipset_1_f13), .F14(graphicchipset_1_f14), .F15(graphicchipset_1_f15), .F16(F16), .F17(F17),
    .F18(F18), .F19(F19), .F20(F20), .F21(F21), .F22(F22), .F23(F23), .F24(F24), .F25(F25), .F26(F26),
    .F27(F27), .F28(F28), .F29(F29), .F30(F30));
  Player player_1 (.in_1(in_3), .out_2(player), .out_3(player_1_out_3));
  assign F3 = bitselector_1_out | graphicchipset_1_f3;  // OR_Gate or_1, 32 bits wide
  assign F4 = bitselector_2_out | graphicchipset_1_f4;  // OR_Gate or_2, 32 bits wide
  assign F5 = bitselector_3_out | graphicchipset_1_f5;  // OR_Gate or_3, 32 bits wide
  assign F6 = bitselector_4_out | graphicchipset_1_f6;  // OR_Gate or_4, 32 bits wide
  assign F7 = bitselector_5_out | graphicchipset_1_f7;  // OR_Gate or_5, 32 bits wide
  assign F8 = bitselector_6_out | graphicchipset_1_f8;  // OR_Gate or_6, 32 bits wide
  assign F9 = bitselector_7_out | graphicchipset_1_f9;  // OR_Gate or_7, 32 bits wide
  assign F10 = bitselector_8_out | graphicchipset_1_f10;  // OR_Gate or_8, 32 bits wide
  assign F11 = bitselector_9_out | graphicchipset_1_f11;  // OR_Gate or_9, 32 bits wide
  assign F12 = bitselector_10_out | graphicchipset_1_f12;  // OR_Gate or_10, 32 bits wide
  assign F13 = bitselector_11_out | graphicchipset_1_f13;  // OR_Gate or_11, 32 bits wide
  assign F14 = bitselector_12_out | graphicchipset_1_f14;  // OR_Gate or_12, 32 bits wide
  assign F15 = bitselector_13_out | graphicchipset_1_f15;  // OR_Gate or_13, 32 bits wide
endmodule

module ReductorDeFrecuencia (
  input  Clock_Entrada,
  output Clock_salida
);

  wire j_k_ff_1_q, j_k_ff_2_q;

  J_K_Flip_Flop j_k_ff_1 (.J(1'b1), .clk(Clock_Entrada), .K(1'b1), .Q(j_k_ff_1_q));  // open: Qn, preset, en, reset
  J_K_Flip_Flop j_k_ff_2 (.J(1'b1), .clk(j_k_ff_1_q), .K(1'b1), .Q(j_k_ff_2_q));  // open: Qn, preset, en, reset
  J_K_Flip_Flop j_k_ff_3 (.J(1'b1), .clk(j_k_ff_2_q), .K(1'b1), .Q(Clock_salida));  // open: Qn, preset, en, reset
endmodule

module GraphicChipSet (
  input  generar_tercero,
  input  [4:0] mover_tercero,
  input  generar_primero,
  input  [4:0] mover_primero,
  input  generar_segundo,
  input  [4:0] mover_segundo,
  output [31:0] F0,
  output [31:0] F1,
  output [31:0] F2,
  output [31:0] F3,
  output [31:0] F4,
  output [31:0] F5,
  output [31:0] F6,
  output [31:0] F7,
  output [31:0] F8,
  output [31:0] F9,
  output [31:0] F10,
  output [31:0] F11,
  output [31:0] F12,
  output [31:0] F13,
  output [31:0] F14,
  output [31:0] F15,
  output [31:0] F16,
  output [31:0] F17,
  output [31:0] F18,
  output [31:0] F19,
  output [31:0] F20,
  output [31:0] F21,
  output [31:0] F22,
  output [31:0] F23,
  output [31:0] F24,
  output [31:0] F25,
  output [31:0] F26,
  output [31:0] F27,
  output [31:0] F28,
  output [31:0] F29,
  output [31:0] F30
);

  wire [7:0] randomsystem_1__8, randomsystem_2__8, randomsystem_3__8;
  wire [9:0] bit_extender_1_out, bit_extender_2_out, demultiplexer_1_out1, demultiplexer_1_out2,
       demultiplexer_1_out3, demultiplexer_1_out4, demultiplexer_1_out5, demultiplexer_1_out6,
       demultiplexer_1_out7, demultiplexer_1_out8, demultiplexer_1_out9, demultiplexer_1_out10,
       demultiplexer_1_out11, demultiplexer_1_out12, demultiplexer_1_out13, demultiplexer_1_out14,
       demultiplexer_1_out15, demultiplexer_1_out16, demultiplexer_1_out17, demultiplexer_1_out18,
       demultiplexer_1_out19, demultiplexer_1_out20, demultiplexer_1_out21, demultiplexer_1_out22,
       demultiplexer_1_out23, demultiplexer_1_out24, demultiplexer_1_out25, demultiplexer_1_out26,
       demultiplexer_1_out27, demultiplexer_1_out28, demultiplexer_1_out29, demultiplexer_1_out30,
       demultiplexer_1_out31, demultiplexer_2_out1, demultiplexer_2_out2, demultiplexer_2_out3,
       demultiplexer_2_out4, demultiplexer_2_out5, demultiplexer_2_out6, demultiplexer_2_out7,
       demultiplexer_2_out8, demultiplexer_2_out9, demultiplexer_2_out10, demultiplexer_2_out11,
       demultiplexer_2_out12, demultiplexer_2_out13, demultiplexer_2_out14, demultiplexer_2_out15,
       demultiplexer_2_out16, demultiplexer_2_out17, demultiplexer_2_out18, demultiplexer_2_out19,
       demultiplexer_2_out20, demultiplexer_2_out21, demultiplexer_2_out22, demultiplexer_2_out23,
       demultiplexer_2_out24, demultiplexer_2_out25, demultiplexer_2_out26, demultiplexer_2_out27,
       demultiplexer_2_out28, demultiplexer_2_out29, demultiplexer_2_out30, demultiplexer_2_out31;
  wire [11:0] bit_extender_3_out, demultiplexer_3_out1, demultiplexer_3_out2, demultiplexer_3_out3,
       demultiplexer_3_out4, demultiplexer_3_out5, demultiplexer_3_out6, demultiplexer_3_out7,
       demultiplexer_3_out8, demultiplexer_3_out9, demultiplexer_3_out10, demultiplexer_3_out11,
       demultiplexer_3_out12, demultiplexer_3_out13, demultiplexer_3_out14, demultiplexer_3_out15,
       demultiplexer_3_out16, demultiplexer_3_out17, demultiplexer_3_out18, demultiplexer_3_out19,
       demultiplexer_3_out20, demultiplexer_3_out21, demultiplexer_3_out22, demultiplexer_3_out23,
       demultiplexer_3_out24, demultiplexer_3_out25, demultiplexer_3_out26, demultiplexer_3_out27,
       demultiplexer_3_out28, demultiplexer_3_out29, demultiplexer_3_out30, demultiplexer_3_out31;

  RandomSystem randomsystem_1 (._2_a_la_3(generar_tercero), ._8(randomsystem_1__8));
  assign bit_extender_1_out = {{2{1'b0}}, randomsystem_1__8};  // Bit_Extender bit_extender_1
  Demultiplexer #(.select(5), .width(10)) demultiplexer_1 (
    .out1(demultiplexer_1_out1), .out2(demultiplexer_1_out2), .out3(demultiplexer_1_out3),
    .out4(demultiplexer_1_out4), .out5(demultiplexer_1_out5), .out6(demultiplexer_1_out6),
    .out7(demultiplexer_1_out7), .out8(demultiplexer_1_out8), .out9(demultiplexer_1_out9),
    .out10(demultiplexer_1_out10), .out11(demultiplexer_1_out11), .out12(demultiplexer_1_out12),
    .out13(demultiplexer_1_out13), .out14(demultiplexer_1_out14), .out15(demultiplexer_1_out15),
    .out16(demultiplexer_1_out16), .out17(demultiplexer_1_out17), .out18(demultiplexer_1_out18),
    .out19(demultiplexer_1_out19), .out20(demultiplexer_1_out20), .out21(demultiplexer_1_out21),
    .out22(demultiplexer_1_out22), .out23(demultiplexer_1_out23), .out24(demultiplexer_1_out24),
    .out25(demultiplexer_1_out25), .out26(demultiplexer_1_out26), .out27(demultiplexer_1_out27),
    .out28(demultiplexer_1_out28), .out29(demultiplexer_1_out29), .out30(demultiplexer_1_out30),
    .out31(demultiplexer_1_out31), .in(bit_extender_1_out), .sel(mover_tercero));  // open: out0, en
  RandomSystem randomsystem_2 (._2_a_la_3(generar_primero), ._8(randomsystem_2__8));
  RandomSystem randomsystem_3 (._2_a_la_3(generar_segundo), ._8(randomsystem_3__8));
  assign bit_extender_2_out = {{2{1'b0}}, randomsystem_2__8};  // Bit_Extender bit_extender_2
  assign bit_extender_3_out = {{4{1'b0}}, randomsystem_3__8};  // Bit_Extender bit_extender_3
  Demultiplexer #(.select(5), .width(10)) demultiplexer_2 (
    .out1(demultiplexer_2_out1), .out2(demultiplexer_2_out2), .out3(demultiplexer_2_out3),
    .out4(demultiplexer_2_out4), .out5(demultiplexer_2_out5), .out6(demultiplexer_2_out6),
    .out7(demultiplexer_2_out7), .out8(demultiplexer_2_out8), .out9(demultiplexer_2_out9),
    .out10(demultiplexer_2_out10), .out11(demultiplexer_2_out11), .out12(demultiplexer_2_out12),
    .out13(demultiplexer_2_out13), .out14(demultiplexer_2_out14), .out15(demultiplexer_2_out15),
    .out16(demultiplexer_2_out16), .out17(demultiplexer_2_out17), .out18(demultiplexer_2_out18),
    .out19(demultiplexer_2_out19), .out20(demultiplexer_2_out20), .out21(demultiplexer_2_out21),
    .out22(demultiplexer_2_out22), .out23(demultiplexer_2_out23), .out24(demultiplexer_2_out24),
    .out25(demultiplexer_2_out25), .out26(demultiplexer_2_out26), .out27(demultiplexer_2_out27),
    .out28(demultiplexer_2_out28), .out29(demultiplexer_2_out29), .out30(demultiplexer_2_out30),
    .out31(demultiplexer_2_out31), .in(bit_extender_2_out), .sel(mover_primero));  // open: out0, en
  Demultiplexer #(.select(5), .width(12)) demultiplexer_3 (
    .out1(demultiplexer_3_out1), .out2(demultiplexer_3_out2), .out3(demultiplexer_3_out3),
    .out4(demultiplexer_3_out4), .out5(demultiplexer_3_out5), .out6(demultiplexer_3_out6),
    .out7(demultiplexer_3_out7), .out8(demultiplexer_3_out8), .out9(demultiplexer_3_out9),
    .out10(demultiplexer_3_out10), .out11(demultiplexer_3_out11), .out12(demultiplexer_3_out12),
    .out13(demultiplexer_3_out13), .out14(demultiplexer_3_out14), .out15(demultiplexer_3_out15),
    .out16(demultiplexer_3_out16), .out17(demultiplexer_3_out17), .out18(demultiplexer_3_out18),
    .out19(demultiplexer_3_out19), .out20(demultiplexer_3_out20), .out21(demultiplexer_3_out21),
    .out22(demultiplexer_3_out22), .out23(demultiplexer_3_out23), .out24(demultiplexer_3_out24),
    .out25(demultiplexer_3_out25), .out26(demultiplexer_3_out26), .out27(demultiplexer_3_out27),
    .out28(demultiplexer_3_out28), .out29(demultiplexer_3_out29), .out30(demultiplexer_3_out30),
    .out31(demultiplexer_3_out31), .in(bit_extender_3_out), .sel(mover_segundo));  // open: out0, en
  GraphicProcessor graphicprocessor_1 (
    ._0_down(demultiplexer_1_out1), ._1_3(demultiplexer_1_out2), ._2_3(demultiplexer_1_out3),
    ._3_3(demultiplexer_1_out4), ._4_3(demultiplexer_1_out5), ._5_3(demultiplexer_1_out6),
    ._6_3(demultiplexer_1_out7), ._7_3(demultiplexer_1_out8), ._8_3(demultiplexer_1_out9),
    ._9_3(demultiplexer_1_out10), ._10_3(demultiplexer_1_out11), ._11_3(demultiplexer_1_out12),
    ._12_3(demultiplexer_1_out13), ._13_3(demultiplexer_1_out14), ._14_3(demultiplexer_1_out15),
    ._15_3(demultiplexer_1_out16), ._16_3(demultiplexer_1_out17), ._17_3(demultiplexer_1_out18),
    ._18_3(demultiplexer_1_out19), ._19_3(demultiplexer_1_out20), ._20_3(demultiplexer_1_out21),
    ._21_3(demultiplexer_1_out22), ._22_3(demultiplexer_1_out23), ._23_3(demultiplexer_1_out24),
    ._24_3(demultiplexer_1_out25), ._25_3(demultiplexer_1_out26), ._26_3(demultiplexer_1_out27),
    ._27_3(demultiplexer_1_out28), ._28_3(demultiplexer_1_out29), ._29_3(demultiplexer_1_out30),
    ._30_3(demultiplexer_1_out31), ._0_8_up(demultiplexer_2_out1), ._1(demultiplexer_2_out2),
    ._2(demultiplexer_2_out3), ._3(demultiplexer_2_out4), ._4(demultiplexer_2_out5),
    ._5(demultiplexer_2_out6), ._6(demultiplexer_2_out7), ._7(demultiplexer_2_out8),
    ._8(demultiplexer_2_out9), ._9(demultiplexer_2_out10), ._10(demultiplexer_2_out11),
    ._11(demultiplexer_2_out12), ._12(demultiplexer_2_out13), ._13(demultiplexer_2_out14),
    ._14(demultiplexer_2_out15), ._15(demultiplexer_2_out16), ._16(demultiplexer_2_out17),
    ._17(demultiplexer_2_out18), ._18(demultiplexer_2_out19), ._19(demultiplexer_2_out20),
    ._20(demultiplexer_2_out21), ._21(demultiplexer_2_out22), ._22(demultiplexer_2_out23),
    ._23(demultiplexer_2_out24), ._24(demultiplexer_2_out25), ._25(demultiplexer_2_out26),
    ._26(demultiplexer_2_out27), ._27(demultiplexer_2_out28), ._28(demultiplexer_2_out29),
    ._29(demultiplexer_2_out30), ._30(demultiplexer_2_out31), .F0(F0), .F1(F1), .F2(F2), .F3(F3), .F4(F4),
    .F5(F5), .F6(F6), .F7(F7), .F8(F8), ._0_16(demultiplexer_3_out1), ._1_2(demultiplexer_3_out2), .F9(F9),
    ._2_2(demultiplexer_3_out3), ._3_2(demultiplexer_3_out4), .F10(F10), ._4_2(demultiplexer_3_out5),
    ._5_2(demultiplexer_3_out6), ._6_2(demultiplexer_3_out7), .F11(F11), ._7_2(demultiplexer_3_out8),
    ._8_2(demultiplexer_3_out9), .F12(F12), ._9_2(demultiplexer_3_out10), ._10_2(demultiplexer_3_out11),
    .F13(F13), ._11_2(demultiplexer_3_out12), ._12_2(demultiplexer_3_out13), .F14(F14),
    ._13_2(demultiplexer_3_out14), ._14_2(demultiplexer_3_out15), ._15_2(demultiplexer_3_out16), .F15(F15),
    ._16_2(demultiplexer_3_out17), ._17_2(demultiplexer_3_out18), .F16(F16), ._18_2(demultiplexer_3_out19),
    ._19_2(demultiplexer_3_out20), .F17(F17), ._20_2(demultiplexer_3_out21), ._21_2(demultiplexer_3_out22),
    .F18(F18), ._22_2(demultiplexer_3_out23), ._23_2(demultiplexer_3_out24), .F19(F19),
    ._24_2(demultiplexer_3_out25), ._25_2(demultiplexer_3_out26), ._26_2(demultiplexer_3_out27), .F20(F20),
    ._27_2(demultiplexer_3_out28), ._28_2(demultiplexer_3_out29), .F21(F21), ._29_2(demultiplexer_3_out30),
    ._30_2(demultiplexer_3_out31), .F22(F22), .F23(F23), .F24(F24), .F25(F25), .F26(F26), .F27(F27),
    .F28(F28), .F29(F29), .F30(F30));
endmodule

module GraphicProcessor (
  input  [9:0] _0_8_up,
  input  [9:0] _2,
  input  [9:0] _4,
  input  [9:0] _6,
  input  [9:0] _8,
  input  [9:0] _10,
  input  [9:0] _12,
  input  [9:0] _14,
  input  [9:0] _16,
  input  [9:0] _18,
  input  [9:0] _20,
  input  [9:0] _22,
  input  [9:0] _24,
  input  [9:0] _26,
  input  [9:0] _28,
  input  [9:0] _30,
  input  [9:0] _1,
  input  [9:0] _3,
  input  [9:0] _5,
  input  [9:0] _7,
  input  [9:0] _9,
  input  [9:0] _11,
  input  [9:0] _13,
  input  [9:0] _15,
  input  [9:0] _17,
  input  [9:0] _19,
  input  [9:0] _21,
  input  [9:0] _23,
  input  [9:0] _25,
  input  [9:0] _27,
  input  [9:0] _29,
  input  [11:0] _0_16,
  input  [11:0] _1_2,
  input  [11:0] _2_2,
  input  [11:0] _3_2,
  input  [11:0] _4_2,
  input  [11:0] _5_2,
  input  [11:0] _6_2,
  input  [11:0] _7_2,
  input  [11:0] _8_2,
  input  [11:0] _9_2,
  input  [11:0] _10_2,
  input  [11:0] _11_2,
  input  [11:0] _12_2,
  input  [11:0] _13_2,
  input  [11:0] _14_2,
  input  [11:0] _15_2,
  input  [11:0] _16_2,
  input  [11:0] _17_2,
  input  [11:0] _18_2,
  input  [11:0] _19_2,
  input  [11:0] _20_2,
  input  [11:0] _21_2,
  input  [11:0] _22_2,
  input  [11:0] _23_2,
  input  [11:0] _24_2,
  input  [11:0] _25_2,
  input  [11:0] _26_2,
  input  [11:0] _27_2,
  input  [11:0] _28_2,
  input  [11:0] _29_2,
  input  [11:0] _30_2,
  input  [9:0] _0_down,
  input  [9:0] _2_3,
  input  [9:0] _4_3,
  input  [9:0] _6_3,
  input  [9:0] _8_3,
  input  [9:0] _10_3,
  input  [9:0] _12_3,
  input  [9:0] _14_3,
  input  [9:0] _16_3,
  input  [9:0] _18_3,
  input  [9:0] _20_3,
  input  [9:0] _22_3,
  input  [9:0] _24_3,
  input  [9:0] _26_3,
  input  [9:0] _28_3,
  input  [9:0] _30_3,
  input  [9:0] _1_3,
  input  [9:0] _3_3,
  input  [9:0] _5_3,
  input  [9:0] _7_3,
  input  [9:0] _9_3,
  input  [9:0] _11_3,
  input  [9:0] _13_3,
  input  [9:0] _15_3,
  input  [9:0] _17_3,
  input  [9:0] _19_3,
  input  [9:0] _21_3,
  input  [9:0] _23_3,
  input  [9:0] _25_3,
  input  [9:0] _27_3,
  input  [9:0] _29_3,
  output [31:0] F0,
  output [31:0] F1,
  output [31:0] F2,
  output [31:0] F3,
  output [31:0] F4,
  output [31:0] F5,
  output [31:0] F6,
  output [31:0] F7,
  output [31:0] F8,
  output [31:0] F9,
  output [31:0] F10,
  output [31:0] F11,
  output [31:0] F12,
  output [31:0] F13,
  output [31:0] F14,
  output [31:0] F15,
  output [31:0] F16,
  output [31:0] F17,
  output [31:0] F18,
  output [31:0] F19,
  output [31:0] F20,
  output [31:0] F21,
  output [31:0] F22,
  output [31:0] F23,
  output [31:0] F24,
  output [31:0] F25,
  output [31:0] F26,
  output [31:0] F27,
  output [31:0] F28,
  output [31:0] F29,
  output [31:0] F30
);


  assign F0 = {_0_8_up, _0_16, _0_down};
  assign F1 = {_1, _1_2, _1_3};
  assign F2 = {_2, _2_2, _2_3};
  assign F3 = {_3, _3_2, _3_3};
  assign F4 = {_4, _4_2, _4_3};
  assign F5 = {_5, _5_2, _5_3};
  assign F6 = {_6, _6_2, _6_3};
  assign F7 = {_7, _7_2, _7_3};
  assign F8 = {_8, _8_2, _8_3};
  assign F9 = {_9, _9_2, _9_3};
  assign F10 = {_10, _10_2, _10_3};
  assign F11 = {_11, _11_2, _11_3};
  assign F12 = {_12, _12_2, _12_3};
  assign F13 = {_13, _13_2, _13_3};
  assign F14 = {_14, _14_2, _14_3};
  assign F15 = {_15, _15_2, _15_3};
  assign F16 = {_16, _16_2, _16_3};
  assign F17 = {_17, _17_2, _17_3};
  assign F18 = {_18, _18_2, _18_3};
  assign F19 = {_19, _19_2, _19_3};
  assign F20 = {_20, _20_2, _20_3};
  assign F21 = {_21, _21_2, _21_3};
  assign F22 = {_22, _22_2, _22_3};
  assign F23 = {_23, _23_2, _23_3};
  assign F24 = {_24, _24_2, _24_3};
  assign F25 = {_25, _25_2, _25_3};
  assign F26 = {_26, _26_2, _26_3};
  assign F27 = {_27, _27_2, _27_3};
  assign F28 = {_28, _28_2, _28_3};
  assign F29 = {_29, _29_2, _29_3};
  assign F30 = {_30, _30_2, _30_3};
endmodule

module ClockProcessor (
  input  reloj,
  output [4:0] mover_uno,
  output [4:0] mover_dos,
  output [4:0] mover_tres,
  output generar_tres,
  output generar_dos,
  output generar_uno
);

  wire controlled_buffer_1_out, controlled_buffer_2_out, controlled_inverter_1_out,
       controlled_inverter_2_out, reductordefrecuencia_1_clock_salida;

  ReductorDeFrecuencia reductordefrecuencia_1 (
    .Clock_Entrada(reloj), .Clock_salida(reductordefrecuencia_1_clock_salida));
  assign controlled_buffer_1_out = controlled_inverter_1_out ? reductordefrecuencia_1_clock_salida : 1'bz;  // Controlled_Buffer controlled_buffer_1
  Comparator #(.width(5)) comparator_1 (.a(mover_dos), .b({5{1'b0}}), .eq(generar_dos));  // open: gt, lt
  Comparator #(.width(5)) comparator_2 (.a(mover_tres), .b({5{1'b0}}), .eq(generar_tres));  // open: gt, lt
  assign controlled_buffer_2_out = controlled_inverter_2_out ? controlled_buffer_1_out : 1'bz;  // Controlled_Buffer controlled_buffer_2
  Counter #(.width(5), .max('h1f)) counter_1 (
    .Q(mover_uno), .clk(reductordefrecuencia_1_clock_salida));  // open: load, D, count, carry, clr
  assign controlled_inverter_1_out = 1'b1 ? ~generar_uno : 1'bz;  // Controlled_Inverter controlled_inverter_1
  Counter #(.width(5), .max('h1f)) counter_2 (
    .Q(mover_dos), .clk(controlled_buffer_1_out));  // open: load, D, count, carry, clr
  assign controlled_inverter_2_out = 1'b1 ? ~generar_dos : 1'bz;  // Controlled_Inverter controlled_inverter_2
  Counter #(.width(5), .max('h1f)) counter_3 (
    .Q(mover_tres), .clk(controlled_buffer_2_out));  // open: load, D, count, carry, clr
  Comparator #(.width(5)) comparator_3 (.a(mover_uno), .b({5{1'b0}}), .eq(generar_uno));  // open: gt, lt
endmodule

module ScreenStart (
  output [31:0] F9,
  output [31:0] F10,
  output [31:0] F11,
  output [31:0] F12,
  output [31:0] F13,
  output [31:0] F14,
  output [31:0] F15,
  output [31:0] F16,
  output [31:0] F17,
  output [31:0] F18,
  output [31:0] F19,
  output [31:0] F20,
  output [31:0] F21
);


  assign F9 = {32{1'b0}};
  assign F10 = 32'h63736276;
  assign F11 = 32'h94245525;
  assign F12 = 32'hf6265525;
  assign F13 = 32'h91246525;
  assign F14 = 32'h97235276;
  assign F15 = {32{1'b0}};
  assign F16 = 32'h722300;
  assign F17 = 32'h555400;
  assign F18 = 32'h655400;
  assign F19 = 32'h455500;
  assign F20 = 32'h425300;
  assign F21 = {32{1'b0}};
endmodule

module contador (
  input  Reloj,
  output [3:0] Decimas,
  output [3:0] unidades
);

  wire comparator_1_gt;
  wire [7:0] counter_1_q;
  wire [7:4] divider_1_out, divider_1_rem;

  Counter counter_1 (.Q(counter_1_q), .clk(Reloj), .clr(comparator_1_gt));  // open: load, D, count, carry
  Divider divider_1 (
    .a(counter_1_q), .b(8'ha), .out({divider_1_out, Decimas}), .rem({divider_1_rem, unidades}));  // open: upper
  Comparator comparator_1 (.a(counter_1_q), .b(8'h63), .gt(comparator_1_gt));  // open: eq, lt
  Hex_Digit_Display hex_digit_display_1 (.value(Decimas));  // open: dp
  Hex_Digit_Display hex_digit_display_2 (.value(unidades));  // open: dp
endmodule

module Colision (
  input  [31:0] asteroid,
  input  [31:0] barra,
  output out_3
);

  wire and_1_out, and_2_out, and_3_out, and_4_out, and_5_out, and_6_out, and_7_out, and_8_out, and_9_out,
       and_10_out, and_11_out, and_12_out, and_13_out, and_14_out, and_15_out, and_16_out, and_17_out,
       and_18_out, and_19_out, and_20_out, and_21_out, and_22_out, and_23_out, and_24_out, and_25_out,
       and_26_out, and_27_out, and_28_out, and_29_out, and_30_out, and_31_out, and_32_out;

  and and_1 (and_1_out, asteroid[0], barra[0]);
  and and_2 (and_2_out, asteroid[1], barra[1]);
  and and_3 (and_3_out, asteroid[2], barra[2]);
  and and_4 (and_4_out, asteroid[3], barra[3]);
  and and_5 (and_5_out, asteroid[4], barra[4]);
  and and_6 (and_6_out, asteroid[5], barra[5]);
  and and_7 (and_7_out, asteroid[6], barra[6]);
  and and_8 (and_8_out, asteroid[7], barra[7]);
  and and_9 (and_9_out, asteroid[8], barra[8]);
  and and_10 (and_10_out, asteroid[9], barra[9]);
  and and_11 (and_11_out, asteroid[10], barra[10]);
  and and_12 (and_12_out, asteroid[11], barra[11]);
  and and_13 (and_13_out, asteroid[12], barra[12]);
  and and_14 (and_14_out, asteroid[13], barra[13]);
  and and_15 (and_15_out, asteroid[14], barra[14]);
  and and_16 (and_16_out, asteroid[15], barra[15]);
  and and_17 (and_17_out, asteroid[16], barra[16]);
  and and_18 (and_18_out, asteroid[17], barra[17]);
  and and_19 (and_19_out, asteroid[18], barra[18]);
  and and_20 (and_20_out, asteroid[19], barra[19]);
  and and_21 (and_21_out, asteroid[20], barra[20]);
  and and_22 (and_22_out, asteroid[21], barra[21]);
  and and_23 (and_23_out, asteroid[22], barra[22]);
  and and_24 (and_24_out, asteroid[23], barra[23]);
  and and_25 (and_25_out, asteroid[24], barra[24]);
  and and_26 (and_26_out, asteroid[25], barra[25]);
  and and_27 (and_27_out, asteroid[26], barra[26]);
  and and_28 (and_28_out, asteroid[27], barra[27]);
  and and_29 (and_29_out, asteroid[28], barra[28]);
  and and_30 (and_30_out, asteroid[29], barra[29]);
  and and_31 (and_31_out, asteroid[30], barra[30]);
  and and_32 (and_32_out, asteroid[31], barra[31]);
  or or_1 (out_3, and_1_out, and_2_out, and_3_out, and_4_out, and_5_out, and_6_out, and_7_out, and_8_out, and_9_out, and_10_out, and_11_out, and_12_out, and_13_out, and_14_out, and_15_out, and_16_out, and_17_out, and_18_out, and_19_out, and_20_out, and_21_out, and_22_out, and_23_out, and_24_out, and_25_out, and_26_out, and_27_out, and_28_out, and_29_out, and_30_out, and_31_out, and_32_out);
endmodule

module ColisionCompleto (
  input  [31:0] Barra,
  input  [31:0] ULTIMA,
  output [3:0] u1,
  output [3:0] u2,
  output _25,
  output GAME_OVER,
  output [3:0] Pc1,
  output [3:0] pc2
);

  wire and_1_out, and_3_out, colision_1_out_3, comparator_1_eq, comparator_2_eq, comparator_3_eq,
       comparator_4_eq, comparator_5_eq, d_ff_1_q, nor_1_out, not_1_out, or_1_out;

  Comparator #(.width(32)) comparator_1 (.a(ULTIMA), .b({32{1'b0}}), .eq(comparator_1_eq));  // open: gt, lt
  not not_1 (not_1_out, comparator_1_eq);
  Colision colision_1 (.asteroid(ULTIMA), .barra(Barra), .out_3(colision_1_out_3));
  nor nor_1 (nor_1_out, colision_1_out_3, not_1_out);
  and and_1 (and_1_out, not_1_out, nor_1_out);
  contador contador_1 (.Reloj(colision_1_out_3), .Decimas(u1), .unidades(u2));
  contador contador_2 (.Reloj(and_1_out), .Decimas(Pc1), .unidades(pc2));
  Comparator #(.width(4)) comparator_2 (.a(u1), .b(4'b0010), .eq(comparator_2_eq));  // open: gt, lt
  Comparator #(.width(4)) comparator_3 (.a(u2), .b(4'b0101), .eq(comparator_3_eq));  // open: gt, lt
  Comparator #(.width(4)) comparator_4 (.a(Pc1), .b(4'b0010), .eq(comparator_4_eq));  // open: gt, lt
  Comparator #(.width(4)) comparator_5 (.a(pc2), .b(4'b0101), .eq(comparator_5_eq));  // open: gt, lt
  and and_2 (_25, comparator_2_eq, comparator_3_eq);
  and and_3 (and_3_out, comparator_4_eq, comparator_5_eq);
  or or_1 (or_1_out, _25, and_3_out);
  D_Flip_Flop d_ff_1 (.clk(or_1_out), .D(1'b1), .Q(d_ff_1_q));  // open: Qn, preset, en, reset
  Multiplexer multiplexer_1 (.in0(1'b0), .in1(1'b1), .out(GAME_OVER), .sel(d_ff_1_q));  // open: en
endmodule

module ganoPerdio (
  input  [31:0] in_1,
  input  [31:0] in_2,
  input  [31:0] in_3,
  input  [31:0] in_4,
  input  [31:0] in_5,
  input  [31:0] in_6,
  input  [31:0] in_7
);

  DotMatrix #(.inputtype("row"), .matrixcols(32)) dotmatrix_1 (
    .row0(in_1), .row1(in_2), .row2(in_3), .row3(in_4), .row4(in_5), .row5(in_6), .row6(in_7));
endmodule

module Pantalla_GAMEOVER (
  input  GAMEOVER,
  input  GANOUSER,
  output [31:0] _0,
  output [31:0] _1,
  output [31:0] _2,
  output [31:0] _3,
  output [31:0] _4
);

  wire GUSER;

  not not_1 (GUSER, GANOUSER);
  Multiplexer #(.width(32)) multiplexer_1 (
    .in0(32'h899244c9), .in1(32'h89924317), .out(_0), .sel(GUSER), .en(GAMEOVER));
  Multiplexer #(.width(32)) multiplexer_2 (
    .in0(32'h5252452d), .in1(32'h525244a2), .out(_1), .sel(GUSER), .en(GAMEOVER));
  Multiplexer #(.width(32)) multiplexer_3 (
    .in0(32'h2252452b), .in1(32'h22524492), .out(_2), .sel(GUSER), .en(GAMEOVER));
  Multiplexer #(.width(32)) multiplexer_4 (
    .in0(32'h22525529), .in1(32'h2252448a), .out(_3), .sel(GUSER), .en(GAMEOVER));
  Multiplexer #(.width(32)) multiplexer_5 (
    .in0(32'h218c28c9), .in1(32'h218c7332), .out(_4), .sel(GUSER), .en(GAMEOVER));

  // Other names for the same wires on the sheet: GOV = GAMEOVER
endmodule

module TAb_AJEDRES (
  output [31:0] _0,
  output [31:0] _1
);


  assign _0 = 32'haaaaaaaa;
  assign _1 = 32'h55555555;
endmodule
